# Fritzing sketch mcp3008 (saved by Fritzing 0.9.3b)
breadboards: 1

parts:
  Raspberry_Pi_1 = Raspberry Pi 3 [part_number=RPI-3-V1.2]
  IC1 = IC, DIP package, 16 pins [chip_label=MCP3008]
  R1 = Photocell (LDR) [package=THT]
  R2 = Resistor [tolerance=±5% resistance=220 package=THT]

nets:
  N1: Raspberry_Pi_1.3v3, IC1.pin15, IC1.pin16, R1.pin_0
  N2: Raspberry_Pi_1.GPIO10, IC1.pin11
  N3: Raspberry_Pi_1.GPIO9, IC1.pin12
  N4: Raspberry_Pi_1.GPIO11, IC1.pin13
  N5: Raspberry_Pi_1.GPIO8, IC1.pin10
  N6: Raspberry_Pi_1.GND, IC1.pin9, IC1.pin14, R2.Pin_1
  N7: IC1.pin3, R1.pin_1, R2.Pin_0
